# Fritzing sketch Farmbot1 (saved by Fritzing 0.9.3b)
breadboards: 1

parts:
  C1 = Electrolytic Capacitor [capacitance=1µF package="100 mil [THT, electrolytic]"]
  M1 = Stepper Motor - Bipolar
  Composant1 = Arduino Mega 2560 (Rev3)
  Pololu_A1 = Pololu A4988 [package=SO16]
  Raspberry_Pi1 = Raspberry Pi B rev2  # not connected
  Composant2 = Soil Moisture Sensor  # not connected

nets:
  N1: C1.+, Pololu_A1.VMOT
  N2: M1.A, Pololu_A1.2B
  N3: M1.C, Pololu_A1.2A
  N4: M1.B, Pololu_A1.1A
  N5: M1.D, Pololu_A1.1B
  5V: Composant1.5V, Pololu_A1.VDD
  N6: Composant1.GND, Pololu_A1.GND#8
  N7: Composant1.D3_PWM, Pololu_A1.DIR
  N8: Composant1.D4_PWM, Pololu_A1.STEP
  N9: Pololu_A1.RESET, Pololu_A1.SLEEP
